# Fritzing sketch Lighthouse sketch (saved by Fritzing 0.9.3b)

parts:
  LED1 = LEDs [package=led10mm]
  micro_USB = USB_MICROB_PLUG [package=micro-b-ra-smt]
  Componente2 = Arduino Pro Mini v13
  S3 = SWITCH-MOMENTARY-2 [package=tactile-switch-1101ne]

nets:
  GND: LED1.C, micro_USB.GND, Componente2.GND
  N1: LED1.A, Componente2.D9_PWM
  N2: micro_USB.VCC, S3.1
  N3: Componente2.VCC, S3.2

notes:
  Switch
  microUSB to Jumper
  Lighthouse w/ LED
  Arduino Pro Mini
